// Logisim project alu.circ as structural Verilog: 1 circuit, main circuit main
module main (
  input  [5:0] Switch__S,
  input  [31:0] X,
  input  [31:0] Y,
  output Signed_Overflow,
  output [31:0] RESULT,
  output Equal
);

  wire add_overflow, adder_2_cout, adder_3_cout, and_1_out, and_2_out, and_3_out, and_4_out, bitpal_out,
       comparator_1_gt, comparator_1_lt, comparator_2_gt, comparator_2_lt, comparator_6_eq, comparator_7_eq,
       comparator_9_eq, slt_out, sltu_out, sub_overflow;
  wire [4:0] bit_extender_2_out, bit_extender_7_out, bit_extender_10_out, Switch;
  wire [5:0] shifter_1_out;
  wire [6:0] cnto_out;
  wire [30:0] bit_extender_8_out, bit_extender_9_out;
  wire [31:0] add_out, addu_out, and_out, bit_extender_3_out, bit_extender_4_out, bit_extender_5_out,
       bit_extender_6_out, or_out, sll_out, sra_out, srl_out, sub_out, subu_out;

  Bit_Extender #(.in_width(6), .out_width(5)) bit_extender_1 (.in(shifter_1_out), .out(Switch));
  Shifter #(.width(6), .shift("rl")) shifter_1 (.in(Switch__S), .\dist (3'b001), .out(shifter_1_out));
  // Probe on X
  // Probe on Y
  Adder #(.width(32)) adder_1 (.a(X), .b(Y), .out(addu_out));  // open: cin, cout
  Subtractor #(.width(32)) subtractor_1 (.a(X), .b(Y), .out(subu_out));  // open: bin, bout
  Comparator #(.width(32)) comparator_1 (
    .a(sub_out), .b({32{1'b0}}), .gt(comparator_1_gt), .lt(comparator_1_lt));  // open: eq
  Comparator #(.width(32)) comparator_2 (.a(X), .b(Y), .gt(comparator_2_gt), .lt(comparator_2_lt));  // open: eq
  Comparator #(.width(32)) comparator_3 (.a(X), .b(Y), .lt(slt_out));  // open: gt, eq
  Shifter #(.width(32)) shifter_2 (.in(X), .\dist (bit_extender_2_out), .out(sll_out));
  Bit_Extender #(.in_width(32), .out_width(5)) bit_extender_2 (.in(Y), .out(bit_extender_2_out));
  assign bit_extender_3_out = {{31{1'b0}}, slt_out};  // Bit_Extender bit_extender_3
  assign bit_extender_4_out = {{31{1'b0}}, sltu_out};  // Bit_Extender bit_extender_4
  assign bit_extender_5_out = {{25{1'b0}}, cnto_out};  // Bit_Extender bit_extender_5
  assign bit_extender_6_out = {{31{1'b0}}, bitpal_out};  // Bit_Extender bit_extender_6
  Subtractor #(.width(32)) subtractor_2 (.a(X), .b(Y), .out(sub_out));  // open: bin, bout
  and and_1 (and_1_out, comparator_1_gt, comparator_2_lt);
  and and_2 (and_2_out, comparator_1_lt, comparator_2_gt);
  or or_1 (sub_overflow, and_1_out, and_2_out);
  Multiplexer #(.select(5), .width(32), .enable("false")) multiplexer_1 (
    .in0(sll_out), .in1(add_out), .in3(addu_out), .in4(srl_out), .in5(sub_out), .in6(sra_out),
    .in7(subu_out), .in9(and_out), .in11(or_out), .in21(bit_extender_3_out), .in23(bit_extender_4_out),
    .in25(bit_extender_5_out), .in29(bit_extender_6_out), .out(RESULT), .sel(Switch));  // open: in2, in8, in10, in12, in13, in14, in15, in16, in17, in18, in19, in20, in22, in24, in26, in27, in28, in30, in31
  Comparator #(.width(16)) comparator_4 (
    .a({X[0], X[1], X[2], X[3], X[4], X[5], X[6], X[7], X[8], X[9], X[10], X[11], X[12], X[13], X[14], X[15]}),
    .b(X[31:16]), .eq(bitpal_out));  // open: gt, lt
  Bit_Extender #(.in_width(32), .out_width(5)) bit_extender_7 (.in(Y), .out(bit_extender_7_out));
  Bit_Extender #(.in_width(32), .out_width(31)) bit_extender_8 (.in(X), .out(bit_extender_8_out));
  Bit_Extender #(.in_width(32), .out_width(31)) bit_extender_9 (.in(Y), .out(bit_extender_9_out));
  Comparator #(.width(32), .mode("unsigned")) comparator_5 (.a(X), .b(Y), .lt(sltu_out));  // open: gt, eq
  Shifter #(.width(32), .shift("lr")) shifter_3 (.in(X), .\dist (bit_extender_7_out), .out(srl_out));
  Comparator #(.width(5)) comparator_6 (.a(Switch), .b(5'b00001), .eq(comparator_6_eq));  // open: gt, lt
  Comparator #(.width(5)) comparator_7 (.a(Switch), .b(5'b00101), .eq(comparator_7_eq));  // open: gt, lt
  Adder #(.width(32)) adder_2 (.a(X), .b(Y), .out(add_out), .cout(adder_2_cout));  // open: cin
  Adder #(.width(31)) adder_3 (.a(bit_extender_8_out), .b(bit_extender_9_out), .cout(adder_3_cout));  // open: out, cin
  and and_3 (and_3_out, comparator_6_eq, add_overflow);
  and and_4 (and_4_out, sub_overflow, comparator_7_eq);
  Comparator #(.width(32)) comparator_8 (.a(X), .b(Y), .eq(Equal));  // open: gt, lt
  Comparator #(.width(1)) comparator_9 (.a(adder_2_cout), .b(adder_3_cout), .eq(comparator_9_eq));  // open: gt, lt
  not not_1 (add_overflow, comparator_9_eq);
  Bit_Extender #(.in_width(32), .out_width(5)) bit_extender_10 (.in(Y), .out(bit_extender_10_out));
  or or_2 (Signed_Overflow, and_3_out, and_4_out);
  BitAdder #(.width(32)) bitadder_1 (.in0(X), .in1(Y), .out(cnto_out));
  Shifter #(.width(32), .shift("ar")) shifter_4 (.in(X), .\dist (bit_extender_10_out), .out(sra_out));
  assign or_out = X | Y;  // OR_Gate or_3, 32 bits wide
  assign and_out = X & Y;  // AND_Gate and_5, 32 bits wide

  // Notes on the sheet:
  //   INPUT to your circuit
  //   Rotate Left & Use Lower 5 bits
  //   For Instruction Selection
  //   INPUTS to your circuit
  //   sub
  //   addu
  //   subu
  //   slt
  //   sll
  //   DON'T CHANGE THE INPUTS AND OUTPUTS! IF YOU DO SO, YOU NEED TO MAKE SURE THE PINS ARE IN THE RIGHT PLACES!
  //   add
  //   bitpal
  //   sltu
  //   srl
  //   Overflow Detection
  //   Only at add / sub Instructions
  //   OUTPUTS of your circuit
  //   cnto
  //   sra
  //   or
  //   and
endmodule
