// Logisim project cpu.circ as structural Verilog: 5 circuits, main circuit main
module main (
  input  [31:0] RS_READ_VALUE,
  input  [31:0] RT_READ_VALUE,
  input  [31:0] INSTRUCTION,
  input  CLOCK,
  input  RESET,
  output [31:0] t0,
  output [31:0] t1,
  output [31:0] t2,
  output [31:0] t3,
  output [4:0] RT,
  output [4:0] RS,
  output [4:0] Write_Register,
  output [31:0] RD_WRITE_VALUE,
  output RD_WRITE_ENABLE,
  output [23:0] FETCH_ADDRESS
);

  wire AccessByte, ALUSrc, BonE, comparator_3_eq, comparator_4_eq, Equal, ExtOp, Inst_jal, Inst_jr, Inst_lui,
       Inst_NOP, IsRtype, Jump, MemtoReg, MemWr, multiplexer_1_out, MyRs, MyRt, not_1_out, not_2_out,
       not_3_out, nPC_MUX_sel, nPC_sel, or_1_out, Overflow, RegDst, run_my_mux_1_writemy, WriteEnable_My;
  wire [1:0] Rs_My, Rt_My, WriteReg_My;
  wire [4:0] Decoder_rs, Decoder_rt, Decoder_writereg, WriteReg_Run_Raw;
  wire [5:0] ALUCtr, Opcode;
  wire [15:0] Imm16;
  wire [23:0] adder_1_out, adder_2_out, bit_extender_1_out, bit_extender_4_out, JumpAddr, multiplexer_2_out,
       multiplexer_3_out, multiplexer_6_out;
  wire [25:0] Decoder_imm;
  wire [25:24] subtractor_1_out;
  wire [31:0] adder_3_out, ALUResult, bit_extender_3_out, bit_extender_5_out, Extender_output, Instruction_t,
       main_1_read_data_1, main_1_read_data_2, main_2_data_mem_out, multiplexer_7_out, multiplexer_8_out,
       register_1_q, RsReadValue, RtReadValue, shifter_1_out, subtractor_2_out, WriteData_Raw;

  not not_1 (not_1_out, Equal);
  Multiplexer #(.enable("false")) multiplexer_1 (.in0(not_1_out), .in1(Equal), .out(multiplexer_1_out), .sel(BonE));
  and and_1 (nPC_MUX_sel, nPC_sel, multiplexer_1_out);
  assign bit_extender_1_out = {{8{Imm16[15]}}, Imm16};  // Bit_Extender bit_extender_1
  Register #(.width(32)) register_1 (.D(Instruction_t), .Q(register_1_q), .clk(CLOCK));  // open: en, clr
  Adder #(.width(24)) adder_1 (.a(FETCH_ADDRESS), .b(24'h1), .out(adder_1_out));  // open: cin, cout
  Adder #(.width(24)) adder_2 (.a(FETCH_ADDRESS), .b(bit_extender_1_out), .out(adder_2_out));  // open: cin, cout
  regfile_main main_1 (
    .Read_register_1(Rt_My), .Read_register_2(Rs_My), .write_register(WriteReg_My),
    .write_data(RD_WRITE_VALUE), .t0_Value(t0), .t1_Value(t1), .t2_Value(t2), .t3_Value(t3), .clock(CLOCK),
    .RegWrite(WriteEnable_My), .Read_Data_1(main_1_read_data_1), .Read_Data_2(main_1_read_data_2));
  Comparator #(.width(32), .mode("unsigned")) comparator_1 (
    .a(register_1_q), .b({32{1'b0}}), .eq(Inst_NOP));  // open: gt, lt
  Comparator #(.width(6), .mode("unsigned")) comparator_2 (.a(Opcode), .b(6'b001111), .eq(Inst_lui));  // open: gt, lt
  Comparator #(.width(6), .mode("unsigned")) comparator_3 (
    .a(Opcode), .b(6'b001000), .eq(comparator_3_eq));  // open: gt, lt
  and and_2 (Inst_jr, comparator_3_eq, IsRtype);
  Comparator #(.width(6), .mode("unsigned")) comparator_4 (
    .a(Opcode), .b(6'b000011), .eq(comparator_4_eq));  // open: gt, lt
  and and_3 (Inst_jal, comparator_4_eq, not_2_out);
  not not_2 (not_2_out, IsRtype);
  Multiplexer #(.width(24), .enable("false")) multiplexer_2 (
    .in0(JumpAddr), .in1(multiplexer_3_out), .out(multiplexer_2_out), .sel(not_3_out));
  Multiplexer #(.width(24), .enable("false")) multiplexer_3 (
    .in0(adder_1_out), .in1(adder_2_out), .out(multiplexer_3_out), .sel(nPC_MUX_sel));
  not not_3 (not_3_out, Jump);
  Multiplexer #(.width(32), .enable("false")) multiplexer_4 (
    .in0(RS_READ_VALUE), .in1(main_1_read_data_2), .out(RsReadValue), .sel(MyRs));
  Multiplexer #(.width(32), .enable("false")) multiplexer_5 (
    .in0(RT_READ_VALUE), .in1(main_1_read_data_1), .out(RtReadValue), .sel(MyRt));
  Decoder Decoder (
    .INSTRUCTION(register_1_q), .IsRtype(IsRtype), .InstCtr(Opcode), .Rt(Decoder_rt), .Rs(Decoder_rs),
    .WriteReg(Decoder_writereg), .Imm(Decoder_imm));
  Subtractor #(.width(26)) subtractor_1 (
    .a(Decoder_imm), .b(26'h100000), .out({subtractor_1_out, JumpAddr}));  // open: bin, bout
  Bit_Extender #(.in_width(26)) bit_extender_2 (.in(Decoder_imm), .out(Imm16));
  Subtractor #(.width(32)) subtractor_2 (.a(RsReadValue), .b(32'h100000), .out(subtractor_2_out));  // open: bin, bout
  assign bit_extender_3_out = {{8{1'b0}}, FETCH_ADDRESS};  // Bit_Extender bit_extender_3
  Bit_Extender #(.in_width(32), .out_width(24)) bit_extender_4 (.in(subtractor_2_out), .out(bit_extender_4_out));
  Run_My_MUX run_my_mux_1 (
    .Rt(Decoder_rt), .Rs(Decoder_rs), .Rd(Decoder_writereg), .RegDst(RegDst), .Rt_Run(RT), .Rt_My(Rt_My),
    .Rs_Run(RS), .Rs_My(Rs_My), .WriteReg_Run(WriteReg_Run_Raw), .WriteReg_My(WriteReg_My), .MyRt(MyRt),
    .MyRs(MyRs), .WriteMy(run_my_mux_1_writemy));
  Adder #(.width(32)) adder_3 (.a(bit_extender_3_out), .b(32'h100000), .out(adder_3_out));  // open: cin, cout
  Multiplexer #(.width(24), .enable("false")) multiplexer_6 (
    .in0(multiplexer_2_out), .in1(bit_extender_4_out), .out(multiplexer_6_out), .sel(Inst_jr));
  mem_main main_2 (
    .Data_Mem_Addr(ALUResult), .Data_Mem_In(RtReadValue), .ACCESS_BYTE(AccessByte), .CLOCK(CLOCK),
    .MEM_WRITE(MemWr), .Data_Mem_Out(main_2_data_mem_out));
  Register #(.width(24)) PC (.D(multiplexer_6_out), .Q(FETCH_ADDRESS), .clk(CLOCK));  // open: en, clr
  Multiplexer #(.width(32), .enable("false")) multiplexer_7 (
    .in0(RtReadValue), .in1(Extender_output), .out(multiplexer_7_out), .sel(ALUSrc));
  Extender Extender (.Imm16(Imm16), .ExtOp(ExtOp), .Output(Extender_output));
  Multiplexer #(.width(32), .enable("false")) multiplexer_8 (
    .in0(ALUResult), .in1(main_2_data_mem_out), .out(multiplexer_8_out), .sel(MemtoReg));
  and and_4 (WriteEnable_My, RD_WRITE_ENABLE, run_my_mux_1_writemy);
  Multiplexer #(.width(5), .enable("false")) multiplexer_9 (
    .in0(WriteReg_Run_Raw), .in1({5{1'b1}}), .out(Write_Register), .sel(Inst_jal));
  Multiplexer #(.width(32), .enable("false")) multiplexer_10 (
    .in0(WriteData_Raw), .in1(adder_3_out), .out(RD_WRITE_VALUE), .sel(Inst_jal));
  alu_main main_3 (
    .X(RsReadValue), .Equal(Equal), .RESULT(ALUResult), .Signed_Overflow(Overflow), .Y(multiplexer_7_out),
    .Switch__S(ALUCtr));
  assign bit_extender_5_out = {{16{1'b0}}, Imm16};  // Bit_Extender bit_extender_5
  or or_1 (or_1_out, Jump, nPC_MUX_sel);
  Shifter #(.width(32)) shifter_1 (.in(bit_extender_5_out), .\dist (5'b10000), .out(shifter_1_out));
  CtrlUnit ctrlunit_1 (
    .Opcode_Funct(Opcode), .nPC_sel(nPC_sel), .RegDst(RegDst), .RegWr(RD_WRITE_ENABLE), .ExtOp(ExtOp),
    .ALUSrc(ALUSrc), .ALUctr(ALUCtr), .MemWr(MemWr), .MemtoReg(MemtoReg), .Jump(Jump), .BonE(BonE),
    .IsRtype(IsRtype), .AccessByte(AccessByte), .IsNOP(Inst_NOP));
  Multiplexer #(.width(32), .enable("false")) multiplexer_11 (
    .in0(INSTRUCTION), .in1({32{1'b0}}), .out(Instruction_t), .sel(or_1_out));
  Multiplexer #(.width(32), .enable("false")) multiplexer_12 (
    .in0(multiplexer_8_out), .in1(shifter_1_out), .out(WriteData_Raw), .sel(Inst_lui));
  LED led_1 (.in(Overflow));

  // Other names for the same wires on the sheet: CLK = CLOCK; FetchAddr[23:0] = FETCH_ADDRESS;
  //   Instruction_Raw[31:0] = INSTRUCTION; Rs_Run[4:0] = RS; Rt_Run[4:0] = RT; WriteData[31:0] = RD_WRITE_VALUE;
  //   RegWr = RD_WRITE_ENABLE; WriteEnable_Run = RD_WRITE_ENABLE; WriteReg_Run[4:0] = Write_Register

  // Notes on the sheet:
  //   These are outputs/inputs from run.circ
  //   NOTICE SignExt here!
  //   Switching from run.circ / 
  //   RegFile-My is such a waste
  //   of precious time QAQ
  //   These are outputs to run.circ
  //   Register File
  //   $ra
  //   NOP
  //   Instruction Unit
  //   ALU
  //   Data Memory
  //   Control
  //   Unit
  //   Cute LED
endmodule

module Extender (
  input  [15:0] Imm16,
  input  ExtOp,
  output [31:0] Output
);

  wire [31:0] bit_extender_1_out, bit_extender_2_out;

  assign bit_extender_1_out = {{16{1'b0}}, Imm16};  // Bit_Extender bit_extender_1
  assign bit_extender_2_out = {{16{Imm16[15]}}, Imm16};  // Bit_Extender bit_extender_2
  Multiplexer #(.width(32), .enable("false")) multiplexer_1 (
    .in0(bit_extender_1_out), .in1(bit_extender_2_out), .out(Output), .sel(ExtOp));

  // Notes on the sheet:
  //   0:zero-extended
  //   1:sign-extended
endmodule

module Decoder (
  input  [31:0] INSTRUCTION,
  output [5:0] InstCtr,
  output [4:0] Rt,
  output [4:0] Rs,
  output [4:0] WriteReg,
  output IsRtype,
  output [25:0] Imm
);

  wire [25:0] bit_extender_1_out;

  Comparator #(.width(6), .mode("unsigned")) comparator_1 (
    .a({6{1'b0}}), .b(INSTRUCTION[31:26]), .eq(IsRtype));  // open: gt, lt
  Multiplexer #(.width(6), .enable("false")) multiplexer_1 (
    .in0(INSTRUCTION[31:26]), .in1(INSTRUCTION[5:0]), .out(InstCtr), .sel(IsRtype));
  assign bit_extender_1_out = {{21{1'b0}}, INSTRUCTION[10:6]};  // Bit_Extender bit_extender_1
  Multiplexer #(.width(26), .enable("false")) multiplexer_2 (
    .in0(INSTRUCTION[25:0]), .in1(bit_extender_1_out), .out(Imm), .sel(IsRtype));

  assign Rs = INSTRUCTION[25:21];
  assign Rt = INSTRUCTION[20:16];
  assign WriteReg = INSTRUCTION[15:11];

  // Other names for the same wires on the sheet: Funct[5:0] = INSTRUCTION[5:0]; Shamt[4:0] = INSTRUCTION[10:6];
  //   Rtype = IsRtype
endmodule

module Run_My_MUX (
  input  RegDst,
  input  [4:0] Rt,
  input  [4:0] Rs,
  input  [4:0] Rd,
  output MyRt,
  output MyRs,
  output [4:0] Rt_Run,
  output [1:0] Rt_My,
  output [4:0] Rs_Run,
  output [1:0] Rs_My,
  output [4:0] WriteReg_Run,
  output [1:0] WriteReg_My,
  output WriteMy
);

  wire comparator_1_gt, comparator_2_lt, comparator_3_gt, comparator_4_lt, comparator_5_gt, comparator_6_lt;
  wire [1:0] bit_extender_3_out;
  wire [4:0] subtractor_1_out, subtractor_2_out, subtractor_3_out;

  Comparator #(.width(5), .mode("unsigned")) comparator_1 (.a(Rt), .b(5'b00111), .gt(comparator_1_gt));  // open: eq, lt
  Comparator #(.width(5), .mode("unsigned")) comparator_2 (.a(Rt), .b(5'b01100), .lt(comparator_2_lt));  // open: gt, eq
  Subtractor #(.width(5)) subtractor_1 (.a(Rt), .b(5'b01000), .out(subtractor_1_out));  // open: bin, bout
  and and_1 (MyRt, comparator_1_gt, comparator_2_lt);
  Bit_Extender #(.in_width(5), .out_width(2)) bit_extender_1 (.in(subtractor_1_out), .out(Rt_My));
  Comparator #(.width(5), .mode("unsigned")) comparator_3 (.a(Rs), .b(5'b00111), .gt(comparator_3_gt));  // open: eq, lt
  Comparator #(.width(5), .mode("unsigned")) comparator_4 (.a(Rs), .b(5'b01100), .lt(comparator_4_lt));  // open: gt, eq
  Subtractor #(.width(5)) subtractor_2 (.a(Rs), .b(5'b01000), .out(subtractor_2_out));  // open: bin, bout
  and and_2 (MyRs, comparator_3_gt, comparator_4_lt);
  Bit_Extender #(.in_width(5), .out_width(2)) bit_extender_2 (.in(subtractor_2_out), .out(Rs_My));
  Subtractor #(.width(5)) subtractor_3 (.a(Rd), .b(5'b01000), .out(subtractor_3_out));  // open: bin, bout
  Bit_Extender #(.in_width(5), .out_width(2)) bit_extender_3 (.in(subtractor_3_out), .out(bit_extender_3_out));
  Multiplexer #(.width(2), .enable("false")) multiplexer_1 (
    .in0(Rt_My), .in1(bit_extender_3_out), .out(WriteReg_My), .sel(RegDst));
  Multiplexer #(.width(5), .enable("false")) multiplexer_2 (.in0(Rt), .in1(Rd), .out(WriteReg_Run), .sel(RegDst));
  Comparator #(.width(5), .mode("unsigned")) comparator_5 (
    .a(WriteReg_Run), .b(5'b00111), .gt(comparator_5_gt));  // open: eq, lt
  Comparator #(.width(5), .mode("unsigned")) comparator_6 (
    .a(WriteReg_Run), .b(5'b01100), .lt(comparator_6_lt));  // open: gt, eq
  and and_3 (WriteMy, comparator_5_gt, comparator_6_lt);

  assign Rs_Run = Rs;
  assign Rt_Run = Rt;
endmodule

// Control Unit
module CtrlUnit (
  input  [5:0] Opcode_Funct,
  input  IsRtype,
  input  IsNOP,
  output nPC_sel,
  output RegDst,
  output RegWr,
  output ExtOp,
  output ALUSrc,
  output [5:0] ALUctr,
  output MemWr,
  output MemtoReg,
  output Jump,
  output BonE,
  output AccessByte
);

  wire and_2_out, and_3_out, and_8_out, and_10_out, and_11_out, and_12_out, and_13_out, and_14_out,
       and_15_out, and_16_out, and_17_out, comparator_1_eq, comparator_2_eq, comparator_3_eq,
       comparator_4_eq, comparator_5_eq, comparator_6_eq, comparator_7_eq, comparator_8_eq, comparator_9_eq,
       comparator_10_eq, comparator_11_eq, comparator_12_eq, comparator_13_eq, comparator_14_eq,
       comparator_15_eq, comparator_16_eq, comparator_17_eq, comparator_18_eq, comparator_19_eq,
       comparator_20_eq, comparator_21_eq, comparator_22_eq, comparator_23_eq, comparator_24_eq,
       comparator_25_eq, not_1_out, not_2_out, not_3_out, not_4_out, not_5_out, not_6_out, not_7_out,
       not_8_out, not_9_out, not_10_out, not_11_out, not_12_out, not_13_out, not_14_out, not_15_out,
       or_1_out, or_2_out, or_3_out, or_4_out, or_5_out, or_6_out, or_9_out;
  wire [1:0] priority_encoder_1_out;
  wire [5:0] multiplexer_1_out;

  Comparator #(.width(6), .mode("unsigned")) comparator_1 (
    .a(Opcode_Funct), .b(6'b000100), .eq(comparator_1_eq));  // open: gt, lt
  not not_1 (not_1_out, IsRtype);
  Comparator #(.width(6), .mode("unsigned")) comparator_2 (
    .a(Opcode_Funct), .b(6'b000100), .eq(comparator_2_eq));  // open: gt, lt
  Comparator #(.width(6), .mode("unsigned")) comparator_3 (
    .a(Opcode_Funct), .b(6'b000101), .eq(comparator_3_eq));  // open: gt, lt
  Comparator #(.width(6), .mode("unsigned")) comparator_4 (
    .a(Opcode_Funct), .b(6'b001000), .eq(comparator_4_eq));  // open: gt, lt
  Comparator #(.width(6), .mode("unsigned")) comparator_5 (
    .a(Opcode_Funct), .b(6'b000010), .eq(comparator_5_eq));  // open: gt, lt
  not not_2 (not_2_out, IsRtype);
  Comparator #(.width(6), .mode("unsigned")) comparator_6 (
    .a(Opcode_Funct), .b(6'b000100), .eq(comparator_6_eq));  // open: gt, lt
  Comparator #(.width(6), .mode("unsigned")) comparator_7 (
    .a(Opcode_Funct), .b(6'b000101), .eq(comparator_7_eq));  // open: gt, lt
  and and_1 (BonE, comparator_1_eq, not_1_out);
  or or_1 (or_1_out, comparator_2_eq, comparator_3_eq);
  not not_3 (not_3_out, IsRtype);
  and and_2 (and_2_out, comparator_4_eq, IsRtype);
  and and_3 (and_3_out, comparator_5_eq, not_2_out);
  not not_4 (not_4_out, IsNOP);
  or or_2 (or_2_out, comparator_6_eq, comparator_7_eq);
  not not_5 (not_5_out, IsRtype);
  and and_4 (nPC_sel, or_1_out, not_3_out);
  not not_6 (not_6_out, or_3_out);
  or or_3 (or_3_out, and_2_out, nPC_sel, and_3_out);
  and and_5 (RegWr, not_6_out, not_4_out);
  and and_6 (nPC_sel, or_2_out, not_5_out);
  Comparator #(.width(6), .mode("unsigned")) comparator_8 (
    .a(Opcode_Funct), .b(6'b100100), .eq(comparator_8_eq));  // open: gt, lt
  Comparator #(.width(6), .mode("unsigned")) comparator_9 (
    .a(Opcode_Funct), .b(6'b100000), .eq(comparator_9_eq));  // open: gt, lt
  Comparator #(.width(6), .mode("unsigned")) comparator_10 (
    .a(Opcode_Funct), .b(6'b100011), .eq(comparator_10_eq));  // open: gt, lt
  not not_7 (not_7_out, IsRtype);
  Comparator #(.width(6), .mode("unsigned")) comparator_11 (
    .a(Opcode_Funct), .b(6'b101011), .eq(comparator_11_eq));  // open: gt, lt
  not not_8 (not_8_out, IsRtype);
  Comparator #(.width(6), .mode("unsigned")) comparator_12 (
    .a(Opcode_Funct), .b({6{1'b0}}), .eq(comparator_12_eq));  // open: gt, lt
  Comparator #(.width(6), .mode("unsigned")) comparator_13 (
    .a(Opcode_Funct), .b(6'b000010), .eq(comparator_13_eq));  // open: gt, lt
  Comparator #(.width(6), .mode("unsigned")) comparator_14 (
    .a(Opcode_Funct), .b(6'b000011), .eq(comparator_14_eq));  // open: gt, lt
  Comparator #(.width(6), .mode("unsigned")) comparator_15 (
    .a(Opcode_Funct), .b(6'b001001), .eq(comparator_15_eq));  // open: gt, lt
  Comparator #(.width(6), .mode("unsigned")) comparator_16 (
    .a(Opcode_Funct), .b(6'b001100), .eq(comparator_16_eq));  // open: gt, lt
  Comparator #(.width(6), .mode("unsigned")) comparator_17 (
    .a(Opcode_Funct), .b(6'b001101), .eq(comparator_17_eq));  // open: gt, lt
  Comparator #(.width(6), .mode("unsigned")) comparator_18 (
    .a(Opcode_Funct), .b(6'b001111), .eq(comparator_18_eq));  // open: gt, lt
  or or_4 (or_4_out, comparator_8_eq, comparator_9_eq);
  and and_7 (AccessByte, or_4_out, not_9_out);
  not not_9 (not_9_out, IsRtype);
  and and_8 (and_8_out, comparator_10_eq, not_7_out);
  and and_9 (MemWr, comparator_11_eq, not_8_out);
  or or_5 (or_5_out, comparator_12_eq, comparator_13_eq, comparator_14_eq);
  and and_10 (and_10_out, or_5_out, IsRtype);
  or or_6 (or_6_out, comparator_15_eq, comparator_16_eq, comparator_17_eq, comparator_18_eq);
  and and_11 (and_11_out, or_6_out, not_10_out);
  not not_10 (not_10_out, IsRtype);
  or or_7 (MemtoReg, and_8_out, AccessByte);
  or or_8 (ALUSrc, ExtOp, and_10_out, and_11_out);
  Comparator #(.width(6), .mode("unsigned")) comparator_19 (
    .a(Opcode_Funct), .b(6'b001001), .eq(comparator_19_eq));  // open: gt, lt
  and and_12 (and_12_out, comparator_19_eq, not_11_out);
  not not_11 (not_11_out, IsRtype);
  Comparator #(.width(6), .mode("unsigned")) comparator_20 (
    .a(Opcode_Funct), .b(6'b000010), .eq(comparator_20_eq));  // open: gt, lt
  or or_9 (or_9_out, comparator_20_eq, comparator_21_eq);
  Comparator #(.width(6), .mode("unsigned")) comparator_21 (
    .a(Opcode_Funct), .b(6'b000011), .eq(comparator_21_eq));  // open: gt, lt
  not not_12 (not_12_out, IsRtype);
  Comparator #(.width(6), .mode("unsigned")) comparator_22 (
    .a(Opcode_Funct), .b(6'b001000), .eq(comparator_22_eq));  // open: gt, lt
  Multiplexer #(.select(2), .width(6), .enable("false")) multiplexer_1 (
    .in0(6'b100000), .in1(6'b100001), .in2(6'b100100), .in3(6'b100101), .out(multiplexer_1_out),
    .sel(priority_encoder_1_out));
  Comparator #(.width(6), .mode("unsigned")) comparator_23 (
    .a(Opcode_Funct), .b(6'b001001), .eq(comparator_23_eq));  // open: gt, lt
  and and_13 (and_13_out, comparator_23_eq, not_13_out);
  not not_13 (not_13_out, IsRtype);
  Comparator #(.width(6), .mode("unsigned")) comparator_24 (
    .a(Opcode_Funct), .b(6'b001100), .eq(comparator_24_eq));  // open: gt, lt
  and and_14 (and_14_out, comparator_24_eq, not_14_out);
  not not_14 (not_14_out, IsRtype);
  Comparator #(.width(6), .mode("unsigned")) comparator_25 (
    .a(Opcode_Funct), .b(6'b001101), .eq(comparator_25_eq));  // open: gt, lt
  and and_15 (and_15_out, comparator_25_eq, not_15_out);
  not not_15 (not_15_out, IsRtype);
  or or_10 (ExtOp, MemtoReg, MemWr, and_12_out);
  and and_16 (and_16_out, or_9_out, not_12_out);
  or or_11 (Jump, and_16_out, and_17_out);
  and and_17 (and_17_out, comparator_22_eq, IsRtype);
  Multiplexer #(.width(6), .enable("false")) multiplexer_2 (
    .in0(multiplexer_1_out), .in1(Opcode_Funct), .out(ALUctr), .sel(IsRtype));
  Priority_Encoder #(.select(2)) priority_encoder_1 (
    .in0(ExtOp), .in1(and_13_out), .in2(and_14_out), .in3(and_15_out), .out(priority_encoder_1_out),
    .en_in(1'b1));  // open: gs, en_out

  assign RegDst = IsRtype;

  // Other names for the same wires on the sheet: Opcode[5:0] = Opcode_Funct
endmodule
