// Logisim project mem-harness.circ as structural Verilog: 1 circuit, main circuit main
module main (
  output [7:0] test_num,
  output [31:0] Data_Mem_Out
);

  wire clock_1_out;
  wire [1:0] rom_3_data;
  wire [7:0] adder_1_out;
  wire [31:0] rom_1_data, rom_2_data;

  Register register_1 (.D(adder_1_out), .en(1'b1), .Q(test_num), .clk(clock_1_out));  // open: clr
  Adder adder_1 (.a(8'h1), .b(test_num), .out(adder_1_out));  // open: cin, cout
  ROM #(.dataWidth(32)) rom_1 (.addr(test_num), .data(rom_1_data));  // open: sel
  ROM #(.dataWidth(32)) rom_2 (.addr(test_num), .data(rom_2_data));  // open: sel
  ROM #(.dataWidth(2)) rom_3 (.addr(test_num), .data(rom_3_data));  // open: sel
  Clock clock_1 (.out(clock_1_out));
  mem_main main_1 (
    .Data_Mem_Addr(rom_1_data), .Data_Mem_In(rom_2_data), .ACCESS_BYTE(rom_3_data[1]), .CLOCK(clock_1_out),
    .MEM_WRITE(rom_3_data[0]), .Data_Mem_Out(Data_Mem_Out));
  // Probe on Data_Mem_Out

  // Notes on the sheet:
  //   contents of rom_1 (hex, n*v repeats v):
  //   10010000 10010004 10010000 10010004
  //   contents of rom_2 (hex, n*v repeats v):
  //   12345678 ff99ff99
  //   contents of rom_3 (hex, n*v repeats v):
  //   1 1 0 2
endmodule
