// Logisim project regfile.circ as structural Verilog: 1 circuit, main circuit main
module main (
  input  [1:0] Read_register_1,
  input  [1:0] Read_register_2,
  input  [1:0] write_register,
  input  [31:0] write_data,
  input  clock,
  input  RegWrite,
  output [31:0] t0_Value,
  output [31:0] t1_Value,
  output [31:0] t2_Value,
  output [31:0] t3_Value,
  output [31:0] Read_Data_1,
  output [31:0] Read_Data_2
);

  wire t1_enable, t2_enable, t3_enable, t4_enable;
  wire [31:0] t1_data, t2_data, t3_data, t4_data;

  Demultiplexer #(.select(2), .width(32)) demultiplexer_1 (
    .out0(t1_data), .out1(t2_data), .out2(t3_data), .out3(t4_data), .in(write_data), .sel(write_register));  // open: en
  Register #(.width(32)) register_1 (.D(t1_data), .en(t1_enable), .Q(t0_Value), .clk(clock));  // open: clr
  Register #(.width(32)) register_2 (.D(t2_data), .en(t2_enable), .Q(t1_Value), .clk(clock));  // open: clr
  Register #(.width(32)) register_3 (.D(t3_data), .en(t3_enable), .Q(t2_Value), .clk(clock));  // open: clr
  Register #(.width(32)) register_4 (.D(t4_data), .en(t4_enable), .Q(t3_Value), .clk(clock));  // open: clr
  Demultiplexer #(.select(2)) demultiplexer_2 (
    .out0(t1_enable), .out1(t2_enable), .out2(t3_enable), .out3(t4_enable), .in(RegWrite),
    .sel(write_register));  // open: en
  Multiplexer #(.select(2), .width(32)) multiplexer_1 (
    .in0(t0_Value), .in1(t1_Value), .in2(t2_Value), .in3(t3_Value), .out(Read_Data_1), .sel(Read_register_1));  // open: en
  Multiplexer #(.select(2), .width(32)) multiplexer_2 (
    .in0(t0_Value), .in1(t1_Value), .in2(t2_Value), .in3(t3_Value), .out(Read_Data_2), .sel(Read_register_2));  // open: en

  // Other names for the same wires on the sheet: CLK = clock; ReadReg1[1:0] = Read_register_1;
  //   ReadReg2[1:0] = Read_register_2; t1_out[31:0] = t0_Value; t2_out[31:0] = t1_Value; t3_out[31:0] = t2_Value;
  //   t4_out[31:0] = t3_Value; WriteReg[1:0] = write_register

  // Notes on the sheet:
  //   These are INPUTS to the circuit
  //   These are INPUTS to the circuit
  //   DO NOT CHANGE THE LOCATIONS OF THE INPUTS/OUTPUTS! IF YOU DO SO, YOU NEED TO MAKE SURE THE PINS ARE AT THE RIGHT PLACE!
  //   These are OUTPUTS to the circuit
  //   Yet again, the clock is not an actual clock, but an input, one that will be driven from a higher circuit
  //   These are OUTPUTS to the circuit
endmodule
