// Logisim project mem.circ as structural Verilog: 2 circuits, main circuit main
module main (
  input  [31:0] Data_Mem_Addr,
  input  [31:0] Data_Mem_In,
  input  ACCESS_BYTE,
  input  CLOCK,
  input  MEM_WRITE,
  output [31:0] Data_Mem_Out
);

  wire not_1_out;
  wire [1:0] Offset;
  wire [7:0] multiplexer_1_out;
  wire [23:0] Vaddr;
  wire [31:0] bit_extender_1_out, DataIn, DataWord, Endian_Inverter_2_output;
  wire [31:26] subtractor_1_out;

  Endian_Inverter Endian_Inverter (.Input(Data_Mem_In), .Output(DataIn));
  Subtractor #(.width(32)) subtractor_1 (
    .a(Data_Mem_Addr), .b(32'h10010000), .out({subtractor_1_out, Vaddr, Offset}));  // open: bin, bout
  not not_1 (not_1_out, MEM_WRITE);
  assign DataWord = MEM_WRITE ? DataIn : 32'bz;  // Controlled_Buffer controlled_buffer_1
  RAM #(.addrWidth(24), .dataWidth(32)) ram_1 (
    .addr(Vaddr), .data(DataWord), .sel(1'b1), .clk(CLOCK), .ld(not_1_out), .clr(1'b0));
  Endian_Inverter Endian_Inverter_2 (.Input(DataWord), .Output(Endian_Inverter_2_output));
  Multiplexer #(.select(2), .width(8), .enable("false")) multiplexer_1 (
    .in0(DataWord[7:0]), .in1(DataWord[15:8]), .in2(DataWord[23:16]), .in3(DataWord[31:24]),
    .out(multiplexer_1_out), .sel(Offset));
  Multiplexer #(.width(32), .enable("false")) multiplexer_2 (
    .in0(Endian_Inverter_2_output), .in1(bit_extender_1_out), .out(Data_Mem_Out), .sel(ACCESS_BYTE));
  assign bit_extender_1_out = {{24{1'b0}}, multiplexer_1_out};  // Bit_Extender bit_extender_1

  // Other names for the same wires on the sheet: AccessByte = ACCESS_BYTE; DataOut[31:0] = Data_Mem_Out

  // Notes on the sheet:
  //   These are INPUTS to the circuit
  //   These are INPUTS to the circuit
  //   DO NOT CHANGE THE LOCATIONS OF THE INPUTS/OUTPUTS! IF YOU DO SO, YOU NEED TO MAKE SURE THE PINS ARE AT THE RIGHT PLACE!
  //   Yet again, the clock is not an actual clock, but an input, one that will be driven from a higher circuit
  //   This is an OUTPUT to the circuit
endmodule

module Endian_Inverter (
  input  [31:0] Input,
  output [31:0] Output
);


  assign Output = {Input[7:0], Input[15:8], Input[23:16], Input[31:24]};
endmodule
